// Digital circuit CPU.dig as structural Verilog
module CPU (
  input  [7:0] Input,
  input  clk,
  output [7:0] Output
);

  wire and_1_out, and_2_out, and_3_out, and_4_out, and_5_out, and_6_out, and_7_out, and_8_out, and_9_out,
       and_10_out, and_11_out, and_12_out, and_13_out, and_14_out, and_15_out, and_16_out, and_17_out,
       and_18_out, and_19_out, and_20_out, and_21_out, and_22_out, and_23_out, and_24_out, and_25_out,
       and_26_out, and_27_out, and_28_out, and_29_out, and_30_out, and_31_out, and_32_out, and_33_out,
       and_34_out, and_35_out, and_36_out, and_37_out, and_38_out, button_1_out, Clk_t, comparator_1_eq,
       comparator_2_eq, delay_1_out, dipswitch_1_out, jk_ff_1_q, jk_ff_2_q, jk_ff_3_q, jk_ff_4_nq, jk_ff_4_q,
       jk_ff_5_q, nClk, not_2_out, not_4_out, not_5_out, not_6_out, not_7_out, not_8_out, not_9_out,
       not_10_out, not_11_out, nRst, or_1_out, or_2_out, or_3_out, or_4_out, or_5_out, or_6_out, or_7_out,
       or_8_out, Proceed, Send_out, xor_1_out;
  wire [7:0] counter8_1_out, Data_d, driver_1_out, not_3_out, rom_1_d;
  wire [15:0] Depth_out, Pointer_out, ProgAddr, register_1_q;

  DipSwitch dipswitch_1 (.out(dipswitch_1_out));
  Button #(.activeLow("true")) nReset (.out(nRst));
  Button button_1 (.out(button_1_out));
  Multiplexer multiplexer_1 (.sel(dipswitch_1_out), .in_0(button_1_out), .in_1(clk), .out(Clk_t));
  not not_1 (nClk, Clk_t);
  or or_1 (or_1_out, Clk_t, or_1_out);
  ROM #(.AddrBits(16), .Bits(8)) rom_1 (.A(ProgAddr), .sel(1'b1), .D(rom_1_d));
  not not_2 (not_2_out, or_1_out);
  and and_1 (and_1_out, nClk, Proceed);
  assign not_3_out = ~rom_1_d;  // Not not_3, 8 bits wide
  or or_2 (or_2_out, jk_ff_3_q, not_2_out);
  JK_FF jk_ff_1 (.J(or_2_out), .C(and_1_out), .K(jk_ff_1_q), .Q(jk_ff_1_q));  // open: nQ
  LED led_1 (.in(jk_ff_1_q));
  and and_2 (and_2_out, rom_1_d[0], rom_1_d[1], not_3_out[2], rom_1_d[3]);
  and and_3 (and_3_out, rom_1_d[0], not_3_out[1], rom_1_d[2], rom_1_d[3]);
  and and_4 (and_4_out, not_3_out[4], rom_1_d[5], not_3_out[6], not_3_out[7]);
  and and_5 (and_5_out, not_3_out[0], not_3_out[1], rom_1_d[2], rom_1_d[3]);
  and and_6 (and_6_out, not_3_out[0], rom_1_d[1], rom_1_d[2], rom_1_d[3]);
  and and_7 (and_7_out, rom_1_d[4], rom_1_d[5], not_3_out[6], not_3_out[7]);
  and and_8 (and_8_out, rom_1_d[4], not_3_out[5], rom_1_d[6], not_3_out[7]);
  JK_FF jk_ff_2 (.J(jk_ff_1_q), .C(and_1_out), .K(jk_ff_2_q), .Q(jk_ff_2_q));  // open: nQ
  LED led_2 (.in(jk_ff_2_q));
  and and_9 (and_9_out, and_2_out, and_4_out);
  and and_10 (and_10_out, and_3_out, and_4_out);
  and and_11 (and_11_out, and_5_out, and_4_out);
  and and_12 (and_12_out, and_6_out, and_4_out);
  and and_13 (and_13_out, and_5_out, and_7_out);
  and and_14 (and_14_out, and_6_out, and_7_out);
  and and_15 (and_15_out, and_2_out, and_8_out);
  and and_16 (and_16_out, and_3_out, and_8_out);
  JK_FF jk_ff_3 (.J(jk_ff_2_q), .C(and_1_out), .K(jk_ff_3_q), .Q(jk_ff_3_q));  // open: nQ
  LED led_3 (.in(jk_ff_3_q));
  LED led_4 (.in(and_9_out));
  LED led_5 (.in(and_10_out));
  LED led_6 (.in(and_11_out));
  LED led_7 (.in(and_12_out));
  LED led_8 (.in(and_13_out));
  LED led_9 (.in(and_14_out));
  and and_17 (and_17_out, jk_ff_1_q, jk_ff_4_nq);
  LED led_10 (.in(and_15_out));
  LED led_11 (.in(and_16_out));
  and and_18 (and_18_out, jk_ff_2_q, jk_ff_4_nq);
  or or_3 (or_3_out, and_9_out, and_10_out);
  and and_19 (and_19_out, and_9_out, and_18_out);
  and and_20 (and_20_out, and_10_out, and_18_out);
  and and_21 (and_21_out, and_18_out, and_11_out);
  and and_22 (and_22_out, and_17_out, and_12_out);
  and and_23 (and_23_out, and_17_out, and_13_out);
  and and_24 (and_24_out, and_17_out, and_14_out);
  and and_25 (and_25_out, jk_ff_3_q, jk_ff_4_nq);
  Comparator #(.Bits(8)) comparator_1 (.a(Data_d), .b({8{1'b0}}), .eq(comparator_1_eq));  // open: gt, lt
  and and_26 (and_26_out, and_17_out, or_3_out);
  and and_27 (and_27_out, and_25_out, or_3_out);
  and and_28 (and_28_out, and_8_out, jk_ff_1_q);
  and and_29 (and_29_out, comparator_1_eq, and_15_out);
  not not_4 (not_4_out, comparator_1_eq);
  or or_4 (or_4_out, and_27_out, and_21_out);
  or or_5 (or_5_out, and_26_out, and_22_out);
  or or_6 (or_6_out, and_29_out, and_30_out);
  and and_30 (and_30_out, not_4_out, and_16_out);
  xor xor_1 (xor_1_out, and_16_out, jk_ff_5_q);
  LED led_12 (.in(or_6_out));
  CounterPreset #(.Bits(16)) Depth (
    .en(and_28_out), .C(Clk_t), .dir(xor_1_out), .in({16{1'b0}}), .ld(1'b0), .clr(1'b0), .out(Depth_out));  // open: ovf
  LED led_13 (.in(and_25_out));
  LED led_14 (.in(and_24_out));
  LED led_15 (.in(and_23_out));
  LED led_16 (.in(or_4_out));
  LED led_17 (.in(or_5_out));
  LED led_18 (.in(and_19_out));
  LED led_19 (.in(and_20_out));
  LED led_20 (.in(and_26_out));
  LED led_21 (.in(and_27_out));
  LED led_22 (.in(and_21_out));
  LED led_23 (.in(and_21_out));
  LED led_24 (.in(and_22_out));
  and and_31 (and_31_out, jk_ff_2_q, and_33_out);
  and and_32 (and_32_out, jk_ff_1_q, and_16_out);
  and and_33 (and_33_out, comparator_2_eq, not_6_out);
  or or_7 (or_7_out, and_25_out, and_37_out);
  or or_8 (or_8_out, and_24_out, and_23_out);
  not not_5 (not_5_out, and_20_out);
  and and_34 (and_34_out, or_6_out, jk_ff_2_q);
  and and_35 (and_35_out, and_32_out, or_6_out);
  not not_6 (not_6_out, or_6_out);
  not not_7 (not_7_out, Clk_t);
  and and_36 (and_36_out, or_6_out, and_28_out);
  CounterPreset #(.Bits(16)) Counter (
    .en(or_7_out), .C(Clk_t), .dir(jk_ff_5_q), .in({16{1'b0}}), .ld(1'b0), .clr(1'b0), .out(ProgAddr));  // open: ovf
  not not_8 (not_8_out, Clk_t);
  CounterPreset #(.Bits(16)) Pointer (
    .en(or_8_out), .C(Clk_t), .dir(and_23_out), .in({16{1'b0}}), .ld(1'b0), .clr(1'b0), .out(Pointer_out));  // open: ovf
  not not_9 (not_9_out, and_19_out);
  Delay delay_1 (.in(and_21_out), .out(delay_1_out));
  not not_10 (not_10_out, delay_1_out);
  JK_FF jk_ff_4 (.J(and_34_out), .C(Clk_t), .K(and_31_out), .Q(jk_ff_4_q), .nQ(jk_ff_4_nq));
  JK_FF jk_ff_5 (.J(and_35_out), .C(not_8_out), .K(and_31_out), .Q(jk_ff_5_q));  // open: nQ
  Register #(.Bits(16)) register_1 (.D(Depth_out), .C(not_7_out), .en(and_36_out), .Q(register_1_q));
  // Probe on ProgAddr
  // Probe on Pointer_out
  RAMDualPort #(.AddrBits(16), .Bits(8)) Data (
    .A(Pointer_out), .Din(driver_1_out), .str(or_4_out), .C(Clk_t), .ld(1'b1), .D(Data_d));
  and and_37 (and_37_out, jk_ff_4_q, jk_ff_3_q);
  // Probe on register_1_q
  Comparator #(.Bits(16)) comparator_2 (.a(register_1_q), .b(Depth_out), .eq(comparator_2_eq));  // open: gt, lt
  // Probe on Depth_out
  not not_11 (not_11_out, and_26_out);
  and and_38 (and_38_out, and_21_out, not_10_out);
  LED led_25 (.in(jk_ff_4_q));
  LED led_26 (.in(jk_ff_5_q));
  // Probe on Data_d
  assign driver_1_out = or_5_out ? Data_d : 8'bz;  // Driver driver_1
  Counter8 counter8_1 (
    .nUp(not_9_out), .nDn(not_5_out), .In(driver_1_out), .nLd(not_11_out), .Clr(1'b0), .Out(counter8_1_out));  // open: nBO
  assign driver_1_out = and_27_out ? counter8_1_out : 8'bz;  // Driver driver_2
  assign driver_1_out = and_21_out ? Input : 8'bz;  // Driver driver_3
  RS_FF_AS rs_ff_as_1 (.S(and_38_out), .R(Send_out), .nQ(Proceed));  // open: Q
  Register #(.Bits(8)) register_2 (.D(driver_1_out), .C(Clk_t), .en(and_22_out), .Q(Output));
  // Probe on counter8_1_out
  Button Send (.out(Send_out));
  LED led_27 (.in(and_22_out));

  // Notes on the sheet:
  //   clk: Hz: 10
  //   + -
  //   , .
  //   < >
  //   [ ]
  //   rom_1 loads program.bf
  //   +
  //   -
  //   ,
  //   .
  //   <
  //   >
  //   [
  //   ]
  //   Counter_Inc
  //   Pointer_Inc
  //   Pointer_Dec
  //   Changer_Add
  //   Changer_Sub
  //   Changer_In
  //   Changer_Out
  //   Input_Out
  //   Input_Await
  //   Output_In
  //   Data_In
  //   Data_Out
  //   Should Trigger
  //   Target Depth
  //   Current Depth
  //   Seek
  //   Dir
endmodule
